// Logisim project ALU.circ as structural Verilog: 2 circuits, main circuit ALU
// ALU\nEncoder
module ALU_Encoder (
  input  add,
  input  \and ,
  input  mult,
  input  addi,
  input  andi,
  input  mulu,
  input  sub,
  input  \or ,
  input  ori,
  input  div,
  input  slt,
  input  slti,
  input  \nor ,
  input  divu,
  input  sltu,
  input  \xor ,
  input  sltui,
  input  xori,
  output [3:0] ALU_Selector
);

  wire add_t, and_t, or_t, slt_t, sltu_t, xor_t;

  or or_1 (add_t, add, addi);
  or or_2 (slt_t, slt, slti);
  or or_3 (sltu_t, sltu, sltui);
  or or_4 (ALU_Selector[0], sub, sltu_t, xor_t, or_t, mulu);
  or or_5 (and_t, \and , andi);
  or or_6 (or_t, \or , ori);
  or or_7 (xor_t, \xor , xori);
  or or_8 (ALU_Selector[1], slt_t, sltu_t, \nor , xor_t, div);
  or or_9 (ALU_Selector[2], and_t, or_t, \nor , xor_t, divu);
  or or_10 (ALU_Selector[3], mult, mulu, div, divu);

  // Other names for the same wires on the sheet: _0 = ALU_Selector[0]; _1 = ALU_Selector[1]; _2 = ALU_Selector[2];
  //   _3 = ALU_Selector[3]; sltiu = sltui
endmodule

module ALU (
  input  [31:0] Data_A,
  input  [31:0] Data_B,
  input  [3:0] Selector,
  input  Clock,
  output [31:0] ALU_Output,
  output [31:0] High,
  output Zero_Flag,
  output Negative_Flag
);

  wire slt_bit, sltu_bit;
  wire [1:0] MiniSelector;
  wire [31:0] Add, And, DivHigh, DivLow, DivuHigh, DivuLow, Low, MultHigh, MultLow, MuluHigh, MuluLow, Nor,
       Operations, Or, slt, sltu, Sub, Xor;

  assign And = Data_A & Data_B;  // AND_Gate and_1, 32 bits wide
  assign Or = Data_A | Data_B;  // OR_Gate or_1, 32 bits wide
  assign Nor = ~(Data_A | Data_B);  // NOR_Gate nor_1, 32 bits wide
  assign Xor = Data_A ^ Data_B;  // XOR_Gate xor_1, 32 bits wide
  or or_2 (MiniSelector[0], Selector[1], Selector[2]);
  or or_3 (MiniSelector[1], Selector[0], Selector[2]);
  Multiplexer #(.select(3), .width(32), .enable("false")) multiplexer_1 (
    .in0(Add), .in1(Sub), .in2(slt), .in3(sltu), .in4(And), .in5(Or), .in6(Nor), .in7(Xor), .out(Operations),
    .sel(Selector[2:0]));
  Adder #(.width(32)) adder_1 (.a(Data_A), .b(Data_B), .out(Add));  // open: cin, cout
  Multiplier #(.width(32)) multiplier_1 (.a(Data_A), .b(Data_B), .out(MuluLow), .cout(MuluHigh));  // open: cin
  Signed_Mult signed_mult_1 (.A(Data_A), .B(Data_B), .Low(MultLow), .High(MultHigh));
  Comparator #(.width(32)) comparator_1 (.a(Data_A), .b(Data_B), .lt(slt_bit));  // open: gt, eq
  assign slt = {{31{1'b0}}, slt_bit};  // Bit_Extender bit_extender_1
  Subtractor #(.width(32)) subtractor_1 (.a(Data_A), .b(Data_B), .out(Sub));  // open: bin, bout
  Divider #(.width(32)) divider_1 (.a(Data_A), .b(Data_B), .out(DivuLow), .rem(DivuHigh));  // open: upper
  Signed_Div signed_div_1 (.A(Data_A), .B(Data_B), .Low(DivLow), .High(DivHigh));
  Comparator #(.width(32), .mode("unsigned")) comparator_2 (.a(Data_A), .b(Data_B), .lt(sltu_bit));  // open: gt, eq
  assign sltu = {{31{1'b0}}, sltu_bit};  // Bit_Extender bit_extender_2
  Multiplexer #(.width(32), .enable("false")) multiplexer_2 (
    .in0(Operations), .in1(Low), .out(ALU_Output), .sel(Selector[3]));
  Multiplexer #(.select(2), .width(32), .enable("false")) multiplexer_3 (
    .in0(MultLow), .in1(DivLow), .in2(MuluLow), .in3(DivuLow), .out(Low), .sel(MiniSelector));
  Multiplexer #(.select(2), .width(32), .enable("false")) multiplexer_4 (
    .in0(MultHigh), .in1(DivHigh), .in2(MuluHigh), .in3(DivuHigh), .out(High), .sel(MiniSelector));
  Comparator #(.width(32)) comparator_3 (
    .a(ALU_Output), .b({32{1'b0}}), .eq(Zero_Flag), .lt(Negative_Flag));  // open: gt

  // Other names for the same wires on the sheet: A[31:0] = Data_A; B[31:0] = Data_B; Clk = Clock;
  //   Output[31:0] = ALU_Output; Selector_t[2:0] = Selector[2:0]; Enable = Selector[3]

  // Notes on the sheet:
  //   Logic operations
  //   Arithmetic operations
endmodule
