// Logisim project PC & Branch Control.circ as structural Verilog: 2 circuits, main circuit Branch Control
module PC (
  input  [31:0] Branch_Control,
  input  Enabled,
  input  Clock,
  input  Reset,
  output [31:0] Instruction
);

  Register #(.width(32)) PC (.D(Branch_Control), .en(Enabled), .Q(Instruction), .clk(Clock), .clr(Reset));
endmodule

// Branch\nControl
module Branch_Control (
  input  beq,
  input  [31:0] PC,
  input  bne,
  input  blez,
  input  [15:0] cte,
  input  bgtz,
  input  bltz,
  input  [25:0] Jump,
  input  j,
  input  jr,
  input  [31:0] Rs,
  input  [31:0] Rt,
  output [31:0] Next_Instruction
);

  wire and_1_out, and_2_out, and_3_out, and_4_out, and_5_out, or_1_out, or_2_out, Rs____0, Rs_____0,
       Rs______Rt;
  wire [1:0] selector;
  wire [31:0] PC____4, PC____4___4___offset;
  wire [31:18] _4___offset;

  or or_1 (or_1_out, Rs_____0, Rs____0);
  and and_1 (and_1_out, beq, Rs______Rt);
  and and_2 (and_2_out, ~Rs______Rt, bne);  // AND_Gate
  and and_3 (and_3_out, blez, or_1_out);
  and and_4 (and_4_out, ~or_1_out, bgtz);  // AND_Gate
  and and_5 (and_5_out, bltz, Rs____0);
  Comparator #(.width(32)) comparator_1 (.a(Rs), .b(Rt), .eq(Rs______Rt));  // open: gt, lt
  assign _4___offset = {{13{cte[15]}}, cte[15]};  // Bit_Extender bit_extender_1
  Adder #(.width(32)) adder_1 (.a(PC), .b(32'h4), .out(PC____4));  // open: cin, cout
  Adder #(.width(32)) adder_2 (
    .a(PC____4), .b({_4___offset, cte, 2'b00}), .out(PC____4___4___offset));  // open: cin, cout
  or or_2 (or_2_out, and_1_out, and_2_out, and_3_out, and_4_out, and_5_out);
  or or_3 (selector[0], j, jr);
  or or_4 (selector[1], or_2_out, jr);
  Comparator #(.width(32)) comparator_2 (.a(Rs), .b({32{1'b0}}), .eq(Rs_____0), .lt(Rs____0));  // open: gt
  Multiplexer #(.select(2), .width(32), .enable("false")) multiplexer_1 (
    .in0(PC____4), .in1({PC[31:28], Jump, 2'b00}), .in2(PC____4___4___offset), .in3(Rs),
    .out(Next_Instruction), .sel(selector));

  // Other names for the same wires on the sheet: _4___offset[17:2] = cte; jump_destiny[31:2] = {PC[31:28], Jump}
endmodule
