// Logisim project RAM Manager.circ as structural Verilog: 3 circuits, main circuit Litle To Big Endian
// Write\nRAM
module Write_RAM (
  input  [31:0] Dir_RAM,
  input  [31:0] Value,
  output [15:0] ADDR,
  output [3:0] Mask,
  output [31:0] Bank_0,
  output [31:0] Bank_1,
  output [31:0] Bank_2,
  output [31:0] Bank_3
);

  wire [31:0] litle_to_big_endian_1_out_2;

  Litle_To_Big_Endian litle_to_big_endian_1 (.in_1(Value), .out_2(litle_to_big_endian_1_out_2));
  Demultiplexer #(.select(2), .width(32), .enable("false")) demultiplexer_1 (
    .out0(Bank_0), .out1(Bank_1), .out2(Bank_2), .out3(Bank_3), .in(litle_to_big_endian_1_out_2),
    .sel(Dir_RAM[3:2]));
  Demultiplexer #(.select(2), .enable("false")) demultiplexer_2 (
    .out0(Mask[0]), .out1(Mask[1]), .out2(Mask[2]), .out3(Mask[3]), .in(1'b1), .sel(Dir_RAM[3:2]));

  assign ADDR = Dir_RAM[19:4];

  // Other names for the same wires on the sheet: selector[1:0] = Dir_RAM[3:2]
endmodule

// Read\nRAM
module Read_RAM (
  input  [31:0] Dir_RAM,
  input  [31:0] Bank_0,
  input  [31:0] Bank_1,
  input  [31:0] Bank_2,
  input  [31:0] Bank_3,
  output [31:0] Value
);

  wire [31:0] multiplexer_1_out;

  Multiplexer #(.select(2), .width(32), .enable("false")) multiplexer_1 (
    .in0(Bank_0), .in1(Bank_1), .in2(Bank_2), .in3(Bank_3), .out(multiplexer_1_out), .sel(Dir_RAM[3:2]));
  Litle_To_Big_Endian litle_to_big_endian_1 (.in_1(multiplexer_1_out), .out_2(Value));

  // Other names for the same wires on the sheet: selector[1:0] = Dir_RAM[3:2]
endmodule

// Litle To\nBig
module Litle_To_Big_Endian (
  input  [31:0] in_1,
  output [31:0] out_2
);


  assign out_2 = {in_1[7:0], in_1[15:8], in_1[23:16], in_1[31:24]};
endmodule
