// Logisim project Register File.circ as structural Verilog: 2 circuits, main circuit Register File
// Register \nFile
module Register_File (
  input  [4:0] Data_Address,
  input  [31:0] Data_In,
  input  [31:0] High,
  input  R_W,
  input  [4:0] Sel_A,
  input  [4:0] Sel_B,
  input  Clock,
  input  Reset,
  input  E_HL,
  input  push,
  input  pop,
  input  E_PC,
  output [31:0] Output_A,
  output [31:0] Output_B,
  output [31:0] High_2,
  output [31:0] Low,
  output [31:0] SP
);

  wire and_1_out, E01, E02, E03, E04, E05, E06, E07, E08, E09, E10, E11, E12, E13, E14, E15, E16, E17, E18,
       E19, E20, E21, E22, E23, E24, E25, E26, E27, E28, E29, E30, E31, E_SP, or_1_out;
  wire [31:0] multiplexer_1_out, Out00, Out01, Out02, Out03, Out04, Out05, Out06, Out07, Out08, Out09, Out10,
       Out11, Out12, Out13, Out14, Out15, Out16, Out17, Out18, Out19, Out20, Out21, Out22, Out23, Out24,
       Out25, Out26, Out27, Out28, Out29, Out30, SP____4, SP____4_t, SP_input;

  Demultiplexer #(.select(5), .enable("false")) demultiplexer_1 (
    .out1(E01), .out2(E02), .out3(E03), .out4(E04), .out5(E05), .out6(E06), .out7(E07), .out8(E08),
    .out9(E09), .out10(E10), .out11(E11), .out12(E12), .out13(E13), .out14(E14), .out15(E15), .out16(E16),
    .out17(E17), .out18(E18), .out19(E19), .out20(E20), .out21(E21), .out22(E22), .out23(E23), .out24(E24),
    .out25(E25), .out26(E26), .out27(E27), .out28(E28), .out29(E29), .out30(E30), .out31(E31), .in(R_W),
    .sel(Data_Address));  // open: out0
  Register #(.width(32)) R00 (.D({32{1'b0}}), .Q(Out00), .clk(Clock), .clr(Reset));  // open: en
  Register #(.width(32)) R04 (.D(Data_In), .en(E04), .Q(Out04), .clk(Clock), .clr(Reset));
  Register #(.width(32)) R08 (.D(Data_In), .en(E08), .Q(Out08), .clk(Clock), .clr(Reset));
  Register #(.width(32)) R12 (.D(Data_In), .en(E12), .Q(Out12), .clk(Clock), .clr(Reset));
  Register #(.width(32)) R16 (.D(Data_In), .en(E16), .Q(Out16), .clk(Clock), .clr(Reset));
  Register #(.width(32)) R20 (.D(Data_In), .en(E20), .Q(Out20), .clk(Clock), .clr(Reset));
  Register #(.width(32)) R24 (.D(Data_In), .en(E24), .Q(Out24), .clk(Clock), .clr(Reset));
  Register #(.width(32)) R28 (.D(Data_In), .en(E28), .Q(Out28), .clk(Clock), .clr(Reset));
  Register #(.width(32)) R01 (.D(Data_In), .en(E01), .Q(Out01), .clk(Clock), .clr(Reset));
  Register #(.width(32)) R05 (.D(Data_In), .en(E05), .Q(Out05), .clk(Clock), .clr(Reset));
  Register #(.width(32)) R09 (.D(Data_In), .en(E09), .Q(Out09), .clk(Clock), .clr(Reset));
  Register #(.width(32)) R13 (.D(Data_In), .en(E13), .Q(Out13), .clk(Clock), .clr(Reset));
  Register #(.width(32)) R17 (.D(Data_In), .en(E17), .Q(Out17), .clk(Clock), .clr(Reset));
  Register #(.width(32)) R21 (.D(Data_In), .en(E21), .Q(Out21), .clk(Clock), .clr(Reset));
  Register #(.width(32)) R25 (.D(Data_In), .en(E25), .Q(Out25), .clk(Clock), .clr(Reset));
  Register #(.width(32)) R29 (.D(Data_In), .en(E29), .Q(Out29), .clk(Clock), .clr(Reset));
  Register #(.width(32)) R02 (.D(Data_In), .en(E02), .Q(Out02), .clk(Clock), .clr(Reset));
  Register #(.width(32)) R06 (.D(Data_In), .en(E06), .Q(Out06), .clk(Clock), .clr(Reset));
  Register #(.width(32)) R10 (.D(Data_In), .en(E10), .Q(Out10), .clk(Clock), .clr(Reset));
  Register #(.width(32)) R14 (.D(Data_In), .en(E14), .Q(Out14), .clk(Clock), .clr(Reset));
  Register #(.width(32)) R18 (.D(Data_In), .en(E18), .Q(Out18), .clk(Clock), .clr(Reset));
  Register #(.width(32)) R22 (.D(Data_In), .en(E22), .Q(Out22), .clk(Clock), .clr(Reset));
  Register #(.width(32)) R26 (.D(Data_In), .en(E26), .Q(Out26), .clk(Clock), .clr(Reset));
  Register #(.width(32)) R30 (.D(Data_In), .en(E30), .Q(Out30), .clk(Clock), .clr(Reset));
  Register #(.width(32)) u_High (.D(High), .en(E_HL), .Q(High_2), .clk(Clock), .clr(Reset));
  Adder #(.width(32)) adder_1 (.a(SP), .b(32'h4), .out(SP____4));  // open: cin, cout
  Multiplexer #(.width(32), .enable("false")) multiplexer_1 (
    .in0(SP____4_t), .in1(SP____4), .out(multiplexer_1_out), .sel(pop));
  Register #(.width(32)) R03 (.D(Data_In), .en(E03), .Q(Out03), .clk(Clock), .clr(Reset));
  Register #(.width(32)) R07 (.D(Data_In), .en(E07), .Q(Out07), .clk(Clock), .clr(Reset));
  Register #(.width(32)) R11 (.D(Data_In), .en(E11), .Q(Out11), .clk(Clock), .clr(Reset));
  Register #(.width(32)) R15 (.D(Data_In), .en(E15), .Q(Out15), .clk(Clock), .clr(Reset));
  Register #(.width(32)) R19 (.D(Data_In), .en(E19), .Q(Out19), .clk(Clock), .clr(Reset));
  Register #(.width(32)) R23 (.D(Data_In), .en(E23), .Q(Out23), .clk(Clock), .clr(Reset));
  Register #(.width(32)) R27 (.D(Data_In), .en(E27), .Q(Out27), .clk(Clock), .clr(Reset));
  Register #(.width(32)) u_Low (.D(Data_In), .en(E_HL), .Q(Low), .clk(Clock), .clr(Reset));
  Multiplexer #(.width(32), .enable("false")) multiplexer_2 (
    .in0(multiplexer_1_out), .in1(Data_In), .out(SP_input), .sel(E31));
  or or_1 (or_1_out, push, pop);
  and and_1 (and_1_out, or_1_out, E_PC);
  Subtractor #(.width(32)) subtractor_1 (.a(SP), .b(32'h4), .out(SP____4_t));  // open: bin, bout
  Register #(.width(32)) u_SP (.D(SP_input), .en(E_SP), .Q(SP), .clk(Clock), .clr(Reset));
  or or_2 (E_SP, Reset, and_1_out, E31);
  Multiplexer #(.select(5), .width(32), .enable("false")) multiplexer_3 (
    .in0(Out00), .in1(Out01), .in2(Out02), .in3(Out03), .in4(Out04), .in5(Out05), .in6(Out06), .in7(Out07),
    .in8(Out08), .in9(Out09), .in10(Out10), .in11(Out11), .in12(Out12), .in13(Out13), .in14(Out14),
    .in15(Out15), .in16(Out16), .in17(Out17), .in18(Out18), .in19(Out19), .in20(Out20), .in21(Out21),
    .in22(Out22), .in23(Out23), .in24(Out24), .in25(Out25), .in26(Out26), .in27(Out27), .in28(Out28),
    .in29(Out29), .in30(Out30), .in31(SP), .out(Output_A), .sel(Sel_A));
  Multiplexer #(.select(5), .width(32), .enable("false")) multiplexer_4 (
    .in0(Out00), .in1(Out01), .in2(Out02), .in3(Out03), .in4(Out04), .in5(Out05), .in6(Out06), .in7(Out07),
    .in8(Out08), .in9(Out09), .in10(Out10), .in11(Out11), .in12(Out12), .in13(Out13), .in14(Out14),
    .in15(Out15), .in16(Out16), .in17(Out17), .in18(Out18), .in19(Out19), .in20(Out20), .in21(Out21),
    .in22(Out22), .in23(Out23), .in24(Out24), .in25(Out25), .in26(Out26), .in27(Out27), .in28(Out28),
    .in29(Out29), .in30(Out30), .in31(SP), .out(Output_B), .sel(Sel_B));

  // Other names for the same wires on the sheet: Clk = Clock; DataAddress[4:0] = Data_Address; DataIn[31:0] = Data_In;
  //   High_Input[31:0] = High; High_t[31:0] = High_2; Rst = Reset; SelectA[4:0] = Sel_A; SelectB[4:0] = Sel_B

  // Notes on the sheet:
  //   Inputs
  //   Outputs
endmodule

// RF\nInput
module RF_Input (
  input  rnd,
  input  [31:0] RAM,
  input  kbd,
  input  mfhi,
  input  [31:0] ALU_Output,
  input  mflo,
  input  pop,
  input  [6:0] Keyboard,
  input  lw,
  input  Clock,
  input  [31:0] High,
  input  KBD_AVAIL,
  input  [31:0] Low,
  output [31:0] RF_Input
);

  wire ram_t;
  wire [2:0] selector;
  wire [31:0] KBD_in, random;

  or or_1 (ram_t, pop, lw);
  or or_2 (selector[0], kbd, ram_t, mflo);
  or or_3 (selector[1], rnd, ram_t);
  or or_4 (selector[2], mfhi, mflo);
  Random #(.width(32)) u_Rnd (.clk(Clock), .next(rnd), .out(random));  // open: clr
  Multiplexer #(.width(32), .enable("false")) multiplexer_1 (
    .in0({32{1'b1}}), .in1({{25{1'b0}}, Keyboard}), .out(KBD_in), .sel(KBD_AVAIL));
  Multiplexer #(.select(3), .width(32), .enable("false")) multiplexer_2 (
    .in0(ALU_Output), .in1(KBD_in), .in2(random), .in3(RAM), .in4(High), .in5(Low), .out(RF_Input),
    .sel(selector));  // open: in6, in7

  // Other names for the same wires on the sheet: ALU[31:0] = ALU_Output; clk = Clock; KBD_t[6:0] = Keyboard
endmodule
