// Logisim project Signed Mult & Div.circ as structural Verilog: 3 circuits, main circuit Aux negator
// sig\nmult
module Signed_Mult (
  input  [31:0] A,
  input  [31:0] B,
  output [31:0] Low,
  output [31:0] High
);

  wire A_Negat, adder_1_cout, B_Negat, Result_Neg;
  wire [31:0] adder_1_out, adder_2_out, aux_negator_1_output, aux_negator_2_output, multiplexer_1_out,
       multiplexer_2_out, multiplier_1_cout, multiplier_1_out, negator_1_out, negator_2_out;

  Comparator #(.width(1), .mode("unsigned")) comparator_1 (.a(1'b1), .b(A[31]), .eq(A_Negat));  // open: gt, lt
  Negator #(.width(32)) negator_1 (.in(A), .out(negator_1_out));
  Negator #(.width(32)) negator_2 (.in(B), .out(negator_2_out));
  Comparator #(.width(1)) comparator_2 (.a(B[31]), .b(1'b1), .eq(B_Negat));  // open: gt, lt
  Multiplexer #(.width(32), .enable("false")) multiplexer_1 (
    .in0(A), .in1(negator_1_out), .out(multiplexer_1_out), .sel(A_Negat));
  Multiplexer #(.width(32), .enable("false")) multiplexer_2 (
    .in0(B), .in1(negator_2_out), .out(multiplexer_2_out), .sel(B_Negat));
  xor xor_1 (Result_Neg, A_Negat, B_Negat);
  Multiplier #(.width(32)) multiplier_1 (
    .a(multiplexer_1_out), .b(multiplexer_2_out), .out(multiplier_1_out), .cout(multiplier_1_cout));  // open: cin
  Aux_negator aux_negator_1 (.Number(multiplier_1_out), .Output(aux_negator_1_output));
  Aux_negator aux_negator_2 (.Number(multiplier_1_cout), .Output(aux_negator_2_output));
  Adder #(.width(32)) adder_1 (
    .a(aux_negator_1_output), .b(32'h1), .out(adder_1_out), .cout(adder_1_cout));  // open: cin
  Adder #(.width(32)) adder_2 (
    .a(aux_negator_2_output), .b({32{1'b0}}), .out(adder_2_out), .cin(adder_1_cout));  // open: cout
  Multiplexer #(.width(32), .enable("false")) multiplexer_3 (
    .in0(multiplier_1_out), .in1(adder_1_out), .out(Low), .sel(Result_Neg));
  Multiplexer #(.width(32), .enable("false")) multiplexer_4 (
    .in0(multiplier_1_cout), .in1(adder_2_out), .out(High), .sel(Result_Neg));
endmodule

// aux \n negat
module Aux_negator (
  input  [31:0] Number,
  output [31:0] Output
);

  not not_1 (Output[0], Number[0]);
  not not_2 (Output[1], Number[1]);
  not not_3 (Output[2], Number[2]);
  not not_4 (Output[3], Number[3]);
  not not_5 (Output[4], Number[4]);
  not not_6 (Output[5], Number[5]);
  not not_7 (Output[6], Number[6]);
  not not_8 (Output[7], Number[7]);
  not not_9 (Output[8], Number[8]);
  not not_10 (Output[9], Number[9]);
  not not_11 (Output[10], Number[10]);
  not not_12 (Output[11], Number[11]);
  not not_13 (Output[12], Number[12]);
  not not_14 (Output[13], Number[13]);
  not not_15 (Output[14], Number[14]);
  not not_16 (Output[15], Number[15]);
  not not_17 (Output[16], Number[16]);
  not not_18 (Output[17], Number[17]);
  not not_19 (Output[18], Number[18]);
  not not_20 (Output[19], Number[19]);
  not not_21 (Output[20], Number[20]);
  not not_22 (Output[21], Number[21]);
  not not_23 (Output[22], Number[22]);
  not not_24 (Output[23], Number[23]);
  not not_25 (Output[24], Number[24]);
  not not_26 (Output[25], Number[25]);
  not not_27 (Output[26], Number[26]);
  not not_28 (Output[27], Number[27]);
  not not_29 (Output[28], Number[28]);
  not not_30 (Output[29], Number[29]);
  not not_31 (Output[30], Number[30]);
  not not_32 (Output[31], Number[31]);
endmodule

// sig\ndiv
module Signed_Div (
  input  [31:0] A,
  input  [31:0] B,
  output [31:0] Low,
  output [31:0] High
);

  wire A_Negat, B_Negat, rest___zero;
  wire [31:0] A____B, A___B, \const , divider_1_rem, minus_A____B, minus_A___B, multiplexer_1_out,
       multiplexer_2_out, negator_2_out, negator_3_out, signed_mult_1_low;

  Negator #(.width(32)) negator_1 (.in(A___B), .out(A____B));
  Comparator #(.width(1), .mode("unsigned")) comparator_1 (.a(1'b1), .b(A[31]), .eq(A_Negat));  // open: gt, lt
  Negator #(.width(32)) negator_2 (.in(A), .out(negator_2_out));
  Negator #(.width(32)) negator_3 (.in(B), .out(negator_3_out));
  Comparator #(.width(1)) comparator_2 (.a(B[31]), .b(1'b1), .eq(B_Negat));  // open: gt, lt
  Multiplexer #(.width(32), .enable("false")) multiplexer_1 (
    .in0(A), .in1(negator_2_out), .out(multiplexer_1_out), .sel(A_Negat));
  Multiplexer #(.width(32), .enable("false")) multiplexer_2 (
    .in0(B), .in1(negator_3_out), .out(multiplexer_2_out), .sel(B_Negat));
  Divider #(.width(32)) divider_1 (
    .a(multiplexer_1_out), .b(multiplexer_2_out), .out(A___B), .rem(divider_1_rem));  // open: upper
  Adder #(.width(32)) adder_1 (.a(A___B), .b(\const ), .out(minus_A____B));  // open: cin, cout
  Comparator #(.width(32)) comparator_3 (.a(divider_1_rem), .b({32{1'b0}}), .eq(rest___zero));  // open: gt, lt
  Multiplexer #(.width(32), .enable("false")) multiplexer_3 (
    .in0(32'h1), .in1({32{1'b0}}), .out(\const ), .sel(rest___zero));
  Negator #(.width(32)) negator_4 (.in(minus_A____B), .out(minus_A___B));
  Signed_Mult signed_mult_1 (.A(B), .B(Low), .Low(signed_mult_1_low));  // open: High
  Multiplexer #(.select(2), .width(32), .enable("false")) multiplexer_4 (
    .in0(A___B), .in1(A____B), .in2(minus_A___B), .in3(minus_A____B), .out(Low), .sel({A_Negat, B_Negat}));
  Subtractor #(.width(32)) subtractor_1 (.a(A), .b(signed_mult_1_low), .out(High));  // open: bin, bout

  // Other names for the same wires on the sheet: result[31:0] = Low; selector[1:0] = {A_Negat, B_Negat}
endmodule
