// Logisim project s-mips.circ as structural Verilog: 8 circuits, main circuit S-MIPS Board
module S_MIPS_Board (
  input  DESHABILITAR_DISPATCHER,
  output halt
);

  wire button_1_out, CLK, CS, d_ff_1_q, LCLR, LoadRAM, LoadRAMOn, LW, R_R_W, R_W, ram_dispatcher_1_finished,
       RCS, Reset_out, RST, TTY_EN;
  wire [2:0] KDB;
  wire [3:0] LMask, Mask, ram_1_read_time, ram_1_write_time, RMask;
  wire [6:0] KDB_DATA, TTY_DATA;
  wire [15:0] Addr, LAddr, RAddr;
  wire [31:0] I0, I1, I2, I3, LData, ram_1_data_out_0, ram_1_data_out_1, ram_1_data_out_2, ram_1_data_out_3,
       RI0, RI1, RI2, RI3;

  TTY #(.rows(25), .cols(80)) tty_1 (.data(TTY_DATA), .clk(CLK), .we(TTY_EN), .clr(RST));
  not not_1 (LoadRAMOn, ram_dispatcher_1_finished);
  RAM_Dispatcher ram_dispatcher_1 (
    .WriteTime(ram_1_write_time), .Clock(CLK), .Data(LData), .Address(LAddr), .Mask(LMask),
    .Finished(ram_dispatcher_1_finished), .Write(LW), .CLR(LCLR));
  Keyboard #(.buflen(64)) keyboard_1 (.clk(CLK), .re(KDB[0]), .avail(KDB[2]), .data(KDB_DATA));  // open: clr
  RAM ram_1 (
    .Address(RAddr), .Data_Out_0(ram_1_data_out_0), .Data_Out_1(ram_1_data_out_1),
    .Data_Out_2(ram_1_data_out_2), .Data_Out_3(ram_1_data_out_3), .Data_In_0(RI0), .Data_In_1(RI1),
    .Data_In_2(RI2), .Data_In_3(RI3), .Mask(RMask), .nRead_Write(R_R_W), .Chip_Select(RCS),
    .Read_Time(ram_1_read_time), .Reset(button_1_out), .Write_Time(ram_1_write_time));
  Button button_1 (.out(button_1_out));
  D_Flip_Flop d_ff_1 (.clk(CLK), .D(1'b1), .Q(d_ff_1_q), .reset(Reset_out));  // open: Qn, preset, en
  Button Reset (.out(Reset_out));
  S_MIPS s_mips_1 (
    .Kbd_Enable(KDB[0]), .Address(Addr), .Kbd_Clear(KDB[1]), .Kbd_Available(KDB[2]), .RAM_In_0(I0),
    .Kbd_ASCII_Data(KDB_DATA), .RAM_In_1(I1), .TTY_Enable(TTY_EN), .RAM_In_2(I2), .RAM_In_3(I3),
    .TTY_ASCII_Data(TTY_DATA), .Reset(RST), .RAM_Out_0(ram_1_data_out_0), .Clock(CLK),
    .RAM_Out_1(ram_1_data_out_1), .Stop(halt), .RAM_Out_2(ram_1_data_out_2), .RAM_Out_3(ram_1_data_out_3),
    .Mask(Mask), .Read_Time(ram_1_read_time), .Write_Time(ram_1_write_time), .nRead_Write(R_W),
    .Chip_Select(CS));
  D_Flip_Flop d_ff_2 (.clk(CLK), .D(d_ff_1_q), .Qn(LCLR), .reset(Reset_out));  // open: Q, preset, en
  or or_1 (RST, LCLR, LoadRAM);
  Clock clock_1 (.out(CLK));
  Multiplexer #(.width(32), .enable("false")) multiplexer_1 (.in0(I0), .in1(LData), .out(RI0), .sel(LoadRAM));
  Multiplexer #(.width(32), .enable("false")) multiplexer_2 (.in0(I1), .in1(LData), .out(RI1), .sel(LoadRAM));
  Multiplexer #(.width(32), .enable("false")) multiplexer_3 (.in0(I2), .in1(LData), .out(RI2), .sel(LoadRAM));
  Multiplexer #(.width(32), .enable("false")) multiplexer_4 (.in0(I3), .in1(LData), .out(RI3), .sel(LoadRAM));
  and and_1 (LoadRAM, ~DESHABILITAR_DISPATCHER, LoadRAMOn);  // AND_Gate
  Multiplexer #(.width(16), .enable("false")) multiplexer_5 (.in0(Addr), .in1(LAddr), .out(RAddr), .sel(LoadRAM));
  Multiplexer #(.width(4), .enable("false")) multiplexer_6 (.in0(Mask), .in1(LMask), .out(RMask), .sel(LoadRAM));
  Multiplexer #(.enable("false")) multiplexer_7 (.in0(CS), .in1(LW), .out(RCS), .sel(LoadRAM));
  Multiplexer #(.enable("false")) multiplexer_8 (.in0(R_W), .in1(LW), .out(R_R_W), .sel(LoadRAM));

  // Notes on the sheet:
  //   NO MODIFICAR
  //   Keyboard
endmodule

module RAM (
  input  [15:0] Address,
  input  [31:0] Data_In_0,
  input  [31:0] Data_In_1,
  input  [31:0] Data_In_2,
  input  [31:0] Data_In_3,
  input  [3:0] Mask,
  input  nRead_Write,
  input  Chip_Select,
  input  Reset,
  output [31:0] Data_Out_0,
  output [31:0] Data_Out_1,
  output [31:0] Data_Out_2,
  output [31:0] Data_Out_3,
  output [3:0] Read_Time,
  output [3:0] Write_Time
);

  wire and_2_out, and_3_out, and_4_out, and_5_out, and_6_out, and_7_out, and_8_out, and_9_out, Changed, CLK,
       comparator_2_eq, comparator_3_eq, comparator_4_eq, comparator_5_eq, comparator_6_eq, Count,
       demultiplexer_3_out0, Idle, Idle_q, Load, Load0, Load1, nand_1_out, or_1_out, or_2_out, or_3_out,
       or_4_out, or_5_out, or_6_out, or_7_out, or_8_out, or_9_out, or_10_out, Proc_q, Update_Mem, Zero_Time;
  wire [3:0] counter_1_q, multiplexer_1_out, subtractor_1_out;
  wire [31:0] register_1_q, register_2_q, register_3_q, register_4_q, register_5_q;

  // Probe on 4'b0011
  // Probe on 4'b0010
  Multiplexer #(.width(4), .enable("false")) multiplexer_1 (
    .in0(4'b0011), .in1(4'b0010), .out(multiplexer_1_out), .sel(nRead_Write));
  or or_1 (or_1_out, Idle, Update_Mem);
  or or_2 (or_2_out, ~Chip_Select, Reset);  // OR_Gate
  Subtractor #(.width(4)) subtractor_1 (.a(multiplexer_1_out), .b(4'b0010), .out(subtractor_1_out));  // open: bin, bout
  Demultiplexer #(.enable("false")) demultiplexer_1 (.out0(Idle), .out1(Load0), .in(Idle_q), .sel(Changed));
  D_Flip_Flop u_Idle (.clk(CLK), .D(or_1_out), .Q(Idle_q), .preset(or_2_out));  // open: Qn, en, reset
  // Probe on counter_1_q
  Counter #(.width(4), .max('hf)) counter_1 (
    .load(Load), .D(subtractor_1_out), .count(Count), .Q(counter_1_q), .clk(CLK), .clr(or_3_out));  // open: carry
  or or_3 (or_3_out, ~Chip_Select, Reset);  // OR_Gate
  Comparator #(.width(4), .mode("unsigned")) comparator_1 (
    .a(4'b0000), .b(counter_1_q), .eq(Zero_Time));  // open: gt, lt
  or or_4 (or_4_out, Count, Load0, Load1);
  Register #(.width(32)) register_1 (.D(Data_In_0), .en(Chip_Select), .Q(register_1_q), .clk(CLK), .clr(or_5_out));
  or or_5 (or_5_out, ~Chip_Select, Reset);  // OR_Gate
  Register #(.width(32)) register_2 (.D(Data_In_1), .en(Chip_Select), .Q(register_2_q), .clk(CLK), .clr(or_6_out));
  or or_6 (or_6_out, ~Chip_Select, Reset);  // OR_Gate
  Register #(.width(32)) register_3 (.D(Data_In_2), .en(Chip_Select), .Q(register_3_q), .clk(CLK), .clr(or_7_out));
  or or_7 (or_7_out, ~Chip_Select, Reset);  // OR_Gate
  Register #(.width(32)) register_4 (.D(Data_In_3), .en(Chip_Select), .Q(register_4_q), .clk(CLK), .clr(or_8_out));
  or or_8 (or_8_out, ~Chip_Select, Reset);  // OR_Gate
  Register #(.width(32)) register_5 (
    .D({{11{1'b1}}, nRead_Write, Mask, Address}), .en(Chip_Select), .Q(register_5_q), .clk(CLK),
    .clr(or_9_out));
  or or_9 (or_9_out, ~Chip_Select, Reset);  // OR_Gate
  D_Flip_Flop Proc (.clk(CLK), .D(or_4_out), .Q(Proc_q), .reset(or_10_out));  // open: Qn, preset, en
  or or_10 (or_10_out, ~Chip_Select, Reset);  // OR_Gate
  Demultiplexer #(.enable("false")) demultiplexer_2 (
    .out0(Count), .out1(Update_Mem), .in(demultiplexer_3_out0), .sel(Zero_Time));
  Demultiplexer #(.enable("false")) demultiplexer_3 (
    .out0(demultiplexer_3_out0), .out1(Load1), .in(Proc_q), .sel(Changed));
  Clock clock_1 (.out(CLK));
  Comparator #(.width(32)) comparator_2 (.a(register_1_q), .b(Data_In_0), .eq(comparator_2_eq));  // open: gt, lt
  Comparator #(.width(32)) comparator_3 (.a(register_2_q), .b(Data_In_1), .eq(comparator_3_eq));  // open: gt, lt
  Comparator #(.width(32)) comparator_4 (.a(register_3_q), .b(Data_In_2), .eq(comparator_4_eq));  // open: gt, lt
  Comparator #(.width(32)) comparator_5 (.a(register_4_q), .b(Data_In_3), .eq(comparator_5_eq));  // open: gt, lt
  Comparator #(.width(32)) comparator_6 (
    .a(register_5_q), .b({{11{1'b1}}, nRead_Write, Mask, Address}), .eq(comparator_6_eq));  // open: gt, lt
  nand nand_1 (nand_1_out, comparator_6_eq, comparator_2_eq, comparator_3_eq, comparator_4_eq, comparator_5_eq);
  and and_1 (Changed, nand_1_out, Chip_Select);
  or or_11 (Load, Count, Load1, Load0);
  and and_2 (and_2_out, Mask[0], Update_Mem, nRead_Write);
  and and_3 (and_3_out, Mask[1], Update_Mem, nRead_Write);
  and and_4 (and_4_out, Mask[2], Update_Mem, nRead_Write);
  and and_5 (and_5_out, Mask[3], Update_Mem, nRead_Write);
  RAM_part #(.addrWidth(16), .dataWidth(32), .bus("separate")) ram_1 (
    .addr(Address), .din(Data_In_0), .data(Data_Out_0), .str(and_2_out), .sel(Chip_Select), .clk(CLK),
    .ld(and_6_out), .clr(Reset));
  and and_6 (and_6_out, ~nRead_Write, Idle);  // AND_Gate
  RAM_part #(.addrWidth(16), .dataWidth(32), .bus("separate")) ram_2 (
    .addr(Address), .din(Data_In_1), .data(Data_Out_1), .str(and_3_out), .sel(Chip_Select), .clk(CLK),
    .ld(and_7_out), .clr(Reset));
  and and_7 (and_7_out, ~nRead_Write, Idle);  // AND_Gate
  RAM_part #(.addrWidth(16), .dataWidth(32), .bus("separate")) ram_3 (
    .addr(Address), .din(Data_In_2), .data(Data_Out_2), .str(and_4_out), .sel(Chip_Select), .clk(CLK),
    .ld(and_8_out), .clr(Reset));
  and and_8 (and_8_out, ~nRead_Write, Idle);  // AND_Gate
  RAM_part #(.addrWidth(16), .dataWidth(32), .bus("separate")) ram_4 (
    .addr(Address), .din(Data_In_3), .data(Data_Out_3), .str(and_5_out), .sel(Chip_Select), .clk(CLK),
    .ld(and_9_out), .clr(Reset));
  and and_9 (and_9_out, ~nRead_Write, Idle);  // AND_Gate

  assign Read_Time = 4'b0011;
  assign Write_Time = 4'b0010;

  // Other names for the same wires on the sheet: M0 = Mask[0]; M1 = Mask[1]; M2 = Mask[2]; M3 = Mask[3];
  //   RW = nRead_Write; CLR = Reset; CS = Chip_Select; Load2 = Count

  // Notes on the sheet:
  //   NO MODIFICAR
  //   excepto quizás los valores RT y WT
  //   BANK0
  //   BANK1
  //   BANK2
  //   BANK3
endmodule

module S_MIPS (
  input  Kbd_Available,
  input  [6:0] Kbd_ASCII_Data,
  input  [31:0] RAM_Out_0,
  input  [31:0] RAM_Out_1,
  input  Reset,
  input  [31:0] RAM_Out_2,
  input  Clock,
  input  [31:0] RAM_Out_3,
  input  [3:0] Read_Time,
  input  [3:0] Write_Time,
  output Kbd_Enable,
  output [15:0] Address,
  output Kbd_Clear,
  output TTY_Enable,
  output [6:0] TTY_ASCII_Data,
  output Stop,
  output [31:0] RAM_In_0,
  output [31:0] RAM_In_1,
  output [31:0] RAM_In_2,
  output [31:0] RAM_In_3,
  output [3:0] Mask,
  output nRead_Write,
  output Chip_Select
);

  wire control_unit_1_e_inst, control_unit_1_e_pc, control_unit_1_read_end, halt, PC_Address, read_RAM,
       write_RAM;
  wire [31:0] Dir_RAM, value_read, value_write;

  Write_RAM write_ram_1 (
    .Dir_RAM(Dir_RAM), .Value(value_write), .ADDR(Address), .Mask(Mask), .Bank_0(RAM_In_0),
    .Bank_1(RAM_In_1), .Bank_2(RAM_In_2), .Bank_3(RAM_In_3));
  CONTROL_UNIT control_unit_1 (
    .Clock(Clock), .Read_RAM(read_RAM), .Reset(Reset), .Write_RAM(write_RAM), .halt(halt),
    .Read_RAM_time(Read_Time), .Write_RAM_time(Write_Time), .E_inst(control_unit_1_e_inst), .CS(Chip_Select),
    .Read_End(control_unit_1_read_end), .R_W(nRead_Write), .E_PC(control_unit_1_e_pc), .End(Stop),
    .PC_Address(PC_Address));
  Read_RAM read_ram_1 (
    .Dir_RAM(Dir_RAM), .Bank_0(RAM_Out_0), .Bank_1(RAM_Out_1), .Bank_2(RAM_Out_2), .Bank_3(RAM_Out_3),
    .Value(value_read));
  DATA_PATH data_path_1 (
    .Clock(Clock), .Instruction(value_read), .Reset(Reset), .E_PC(control_unit_1_e_pc),
    .Keyboard(Kbd_ASCII_Data), .Read_RAM(control_unit_1_read_end), .E_inst(control_unit_1_e_inst),
    .KBD_AVAIL(Kbd_Available), .PC_Address(PC_Address), .Dir_Address(Dir_RAM), .RAM__w(value_write),
    .halt(halt), .Read_RAM_2(read_RAM), .kbd(Kbd_Enable), .Write_RAM(write_RAM), .tty(TTY_Enable),
    .tty_DATA(TTY_ASCII_Data));

  // Other names for the same wires on the sheet: CLK = Clock; CLR = Reset; CS = Chip_Select;
  //   KBD_AVAIL = Kbd_Available; KBD_CLR = Kbd_Clear; KBD_DATA[6:0] = Kbd_ASCII_Data; RAM_A[15:0] = Address;
  //   RAM_INPUT_0[31:0] = RAM_In_0; RAM_INPUT_1[31:0] = RAM_In_1; RAM_INPUT_2[31:0] = RAM_In_2;
  //   RAM_INPUT_3[31:0] = RAM_In_3; RAM_MASK[3:0] = Mask; RAM_OUTPUT_0[31:0] = RAM_Out_0;
  //   RAM_OUTPUT_1[31:0] = RAM_Out_1; RAM_OUTPUT_2[31:0] = RAM_Out_2; RAM_OUTPUT_3[31:0] = RAM_Out_3;
  //   RW = nRead_Write; TTY_DATA[6:0] = TTY_ASCII_Data

  // Notes on the sheet:
  //   RAM ADDRESS
  //   DATA FROM RAM
  //   DATA TO RAM
  //   DATA WRITE MASK
  //   RAM TIMING
  //   RAM CONTROL
  //   KEYBOARD
  //   TTY
  //   SEQUENCING
endmodule

module RAM_Dispatcher (
  input  [3:0] WriteTime,
  input  Clock,
  input  CLR,
  output [31:0] Data,
  output [15:0] Address,
  output [3:0] Mask,
  output Finished,
  output Write
);

  wire demultiplexer_2_out1, demultiplexer_3_out1, End, IDLE_q, IncAddr, Load, or_1_out, or_2_out, While_q,
       WriteEnd;
  wire [3:0] counter_1_q;
  wire [31:0] CurrentAddress_q;

  Counter #(.width(32), .max('hffffffff)) CurrentAddress (
    .count(IncAddr), .Q({CurrentAddress_q[31:18], Address, CurrentAddress_q[1:0]}), .clk(Clock), .clr(CLR));  // open: load, D, carry
  or or_1 (or_1_out, IncAddr, demultiplexer_3_out1, Finished);
  D_Flip_Flop IDLE (.clk(Clock), .D(or_1_out), .Q(IDLE_q), .preset(CLR));  // open: Qn, en, reset
  Demultiplexer #(.enable("false")) demultiplexer_1 (.out0(Load), .out1(Finished), .in(IDLE_q), .sel(End));
  D_Flip_Flop While (.clk(Clock), .D(or_2_out), .Q(While_q), .reset(CLR));  // open: Qn, preset, en
  or or_2 (or_2_out, Write, Load);
  RAM_part #(.addrWidth(18), .dataWidth(32)) ram_1 (
    .addr({Address, CurrentAddress_q[1:0]}), .data(Data), .clk(Clock));  // open: sel, ld, clr
  Demultiplexer #(.enable("false")) demultiplexer_2 (
    .out0(Write), .out1(demultiplexer_2_out1), .in(While_q), .sel(WriteEnd));
  Decoder #(.select(2)) decoder_1 (
    .out0(Mask[0]), .out1(Mask[1]), .out2(Mask[2]), .out3(Mask[3]), .sel(CurrentAddress_q[1:0]));  // open: en
  Demultiplexer #(.enable("false")) demultiplexer_3 (
    .out0(IncAddr), .out1(demultiplexer_3_out1), .in(demultiplexer_2_out1), .sel(End));
  Counter #(.width(4), .max('hf)) counter_1 (
    .load(Load), .D(WriteTime), .count(Write), .Q(counter_1_q), .clk(Clock));  // open: carry, clr
  Comparator #(.width(32)) comparator_1 (.a(Data), .b({32{1'b1}}), .eq(End));  // open: gt, lt
  Comparator #(.width(4)) comparator_2 (.a(4'b0000), .b(counter_1_q), .eq(WriteEnd));  // open: gt, lt

  // Other names for the same wires on the sheet: CLK = Clock; Count = Write; WT[3:0] = WriteTime
endmodule

// DATA\nPATH
module DATA_PATH (
  input  Clock,
  input  [31:0] Instruction,
  input  Reset,
  input  E_PC,
  input  [6:0] Keyboard,
  input  Read_RAM,
  input  E_inst,
  input  KBD_AVAIL,
  input  PC_Address,
  output [31:0] Dir_Address,
  output [31:0] RAM__w,
  output halt,
  output Read_RAM_2,
  output kbd,
  output Write_RAM,
  output tty,
  output [6:0] tty_DATA
);

  wire add, addi, \and , and_1_out, and_2_out, andi, beq, bgtz, blez, bltz, bne, div, divu, E_HL, j, jr, lw,
       mfhi, mflo, mult, mulu, Neg, nop, \nor , \or , or_1_out, or_2_out, or_3_out, or_4_out, or_5_out,
       or_7_out, or_8_out, or_11_out, ori, pop, push, R_W, rnd, slt, slti, sltiu, sltu, sub, sw, tty_t,
       Type_I, \xor , xori, Zero;
  wire [3:0] ALU_Selector;
  wire [4:0] Rd, register_file_1_p9, Rs, Rt;
  wire [15:0] cte;
  wire [25:0] Jump;
  wire [31:0] ALU_Output, B_C, bit_extender_2_out, cte_I15, Hi, High, Lo, multiplexer_2_out,
       multiplexer_4_out, PC, register_1_q, rf_input_1_rf_input, Rt_t, SP;
  wire [31:7] Rs_t;

  or or_1 (or_1_out, add, sub, \and , \or );
  or or_2 (or_2_out, \nor , \xor , slt, sltu);
  or or_3 (or_3_out, mfhi, mflo, addi, andi);
  or or_4 (or_4_out, slti, ori, xori, sltiu);
  or or_5 (or_5_out, rnd, kbd, E_HL);
  or or_6 (E_HL, mult, mulu, div, divu);
  or or_7 (or_7_out, or_1_out, or_2_out, or_3_out, or_4_out, or_5_out);
  and and_1 (and_1_out, E_PC, or_7_out);
  or or_8 (or_8_out, lw, pop);
  and and_2 (and_2_out, or_8_out, Read_RAM);
  or or_9 (R_W, and_1_out, and_2_out);
  Register #(.width(32)) register_1 (.D(Instruction), .en(E_inst), .Q(register_1_q), .clk(Clock), .clr(Reset));
  Instruction_Decoder instruction_decoder_1 (
    .Instruction(register_1_q), .add(add), .\nor (\nor ), .pop(pop), .push(push), .addi(addi), .beq(beq),
    .j(j), .sub(sub), .\xor (\xor ), .andi(andi), .bne(bne), .mult(mult), .slt(slt), .ori(ori), .blez(blez),
    .halt(halt), .rnd(rnd), .mulu(mulu), .sltu(sltu), .xori(xori), .bgtz(bgtz), .tty(tty_t), .kbd(kbd),
    .div(div), .mfhi(mfhi), .slti(slti), .bltz(bltz), .divu(divu), .mflo(mflo), .sltiu(sltiu), .lw(lw),
    .\and (\and ), .nop(nop), .sw(sw), .\or (\or ), .jr(jr), .Jump(Jump), .Const(cte), .Rs(Rs), .Rt(Rt),
    .Rd(Rd), .Type_I(Type_I));
  Branch_Control branch_control_1 (
    .beq(beq), .PC(PC), .bne(bne), .blez(blez), .cte(cte), .bgtz(bgtz), .bltz(bltz), .Jump(Jump), .j(j),
    .jr(jr), .Rs({Rs_t, tty_DATA}), .Rt(Rt_t), .Next_Instruction(B_C));
  and and_3 (tty, tty_t, E_PC);
  PC pc_1 (.Branch_Control(B_C), .Instruction(PC), .Enabled(E_PC), .Clock(Clock), .Reset(Reset));
  RF_Input rf_input_1 (
    .rnd(rnd), .RAM(Instruction), .kbd(kbd), .mfhi(mfhi), .ALU_Output(ALU_Output), .mflo(mflo), .pop(pop),
    .Keyboard(Keyboard), .lw(lw), .Clock(Clock), .High(Hi), .KBD_AVAIL(KBD_AVAIL), .Low(Lo),
    .RF_Input(rf_input_1_rf_input));
  // Register_File register_file_1: pin names not known; wires that end beside it: rf_input_1_rf_input, High, Rs, Rt, push, pop, Read_RAM, Clock, register_file_1_p9, Reset, E_HL, R_W, E_PC, {Rs_t, tty_DATA}, Hi, Rt_t, Lo, SP
  Multiplexer #(.width(5), .enable("false")) multiplexer_1 (.in0(Rd), .in1(Rt), .out(register_file_1_p9), .sel(Type_I));
  ALU_Encoder alu_encoder_1 (
    .add(add), .\and (\and ), .mult(mult), .addi(addi), .andi(andi), .mulu(mulu), .sub(sub), .\or (\or ),
    .ori(ori), .div(div), .slt(slt), .slti(slti), .\nor (\nor ), .divu(divu), .sltu(sltu), .\xor (\xor ),
    .sltui(sltiu), .xori(xori), .ALU_Selector(ALU_Selector));
  or or_10 (Write_RAM, sw, push);
  assign cte_I15 = {{16{cte[15]}}, cte};  // Bit_Extender bit_extender_1
  Multiplexer #(.width(32), .enable("false")) multiplexer_2 (
    .in0(cte_I15), .in1(bit_extender_2_out), .out(multiplexer_2_out), .sel(or_11_out));
  assign bit_extender_2_out = {{16{1'b0}}, cte};  // Bit_Extender bit_extender_2
  or or_11 (or_11_out, andi, ori, xori);
  Multiplexer #(.width(32), .enable("false")) multiplexer_3 (
    .in0({Rs_t, tty_DATA}), .in1(Rt_t), .out(RAM__w), .sel(sw));
  // Probe on Rt_t
  // Probe on {Rs_t, tty_DATA}
  Multiplexer #(.width(32), .enable("false")) multiplexer_4 (
    .in0(Rt_t), .in1(multiplexer_2_out), .out(multiplexer_4_out), .sel(Type_I));
  or or_12 (Read_RAM_2, lw, pop);
  ALU alu_1 (
    .Data_A({Rs_t, tty_DATA}), .Data_B(multiplexer_4_out), .Selector(ALU_Selector), .Clock(Clock),
    .ALU_Output(ALU_Output), .High(High), .Zero_Flag(Zero), .Negative_Flag(Neg));
  RAM_Access ram_access_1 (
    .ALU(ALU_Output), .SP(SP), .PC(PC), .sw(sw), .lw(lw), .pop(pop), .push(push), .PC_Address(PC_Address),
    .Dir_RAM(Dir_Address));

  // Other names for the same wires on the sheet: Clk = Clock; Read__RAM = Read_RAM_2; Rs_t[6:0] = tty_DATA;
  //   Rst = Reset
endmodule

// RAM\nAccess
module RAM_Access (
  input  [31:0] ALU,
  input  [31:0] SP,
  input  [31:0] PC,
  input  sw,
  input  lw,
  input  pop,
  input  push,
  input  PC_Address,
  output [31:0] Dir_RAM
);

  wire [1:0] selector;
  wire [31:0] multiplexer_1_out, subtractor_1_out;

  Multiplexer #(.width(32), .enable("false")) multiplexer_1 (
    .in0(SP), .in1(subtractor_1_out), .out(multiplexer_1_out), .sel(push));
  Subtractor #(.width(32)) subtractor_1 (.a(SP), .b(32'h4), .out(subtractor_1_out));  // open: bin, bout
  or or_1 (selector[1], pop, PC_Address, push);
  or or_2 (selector[0], sw, PC_Address, lw);
  Multiplexer #(.select(2), .width(32), .enable("false")) multiplexer_2 (
    .in0(PC), .in1(ALU), .in2(multiplexer_1_out), .in3(PC), .out(Dir_RAM), .sel(selector));
endmodule

// CONTROL\nUNIT
module CONTROL_UNIT (
  input  Clock,
  input  Read_RAM,
  input  Reset,
  input  Write_RAM,
  input  halt,
  input  [3:0] Read_RAM_time,
  input  [3:0] Write_RAM_time,
  output E_inst,
  output CS,
  output Read_End,
  output R_W,
  output E_PC,
  output End,
  output PC_Address
);

  wire chip_1, chip_2, crono_rst_1, crono_rst_2, demultiplexer_1_out1, demultiplexer_2_out0,
       demultiplexer_3_out0, demultiplexer_4_out0, demultiplexer_4_out1, demultiplexer_5_out0, IDLE_q,
       Load_Inst_q, or_2_out, or_3_out, or_5_out, or_8_out, RAM, RAM_read_load, timer_1_finish,
       timer_2_finish;
  wire [3:0] multiplexer_1_out;

  or or_1 (E_PC, demultiplexer_5_out0, RAM_read_load);
  or or_2 (or_2_out, demultiplexer_5_out0, RAM_read_load, demultiplexer_1_out1);
  D_Flip_Flop d_ff_1 (.clk(Clock), .D(or_3_out), .Q(chip_2), .reset(Reset));  // open: Qn, preset, en
  or or_3 (or_3_out, demultiplexer_2_out0, crono_rst_2);
  Multiplexer #(.width(4), .enable("false")) multiplexer_1 (
    .in0(Read_RAM_time), .in1(Write_RAM_time), .out(multiplexer_1_out), .sel(Write_RAM));
  D_Flip_Flop IDLE (.clk(Clock), .D(or_2_out), .Q(IDLE_q), .preset(Reset));  // open: Qn, en, reset
  Demultiplexer #(.enable("false")) demultiplexer_1 (
    .out0(crono_rst_1), .out1(demultiplexer_1_out1), .in(IDLE_q), .sel(Reset));
  Demultiplexer #(.enable("false")) demultiplexer_2 (
    .out0(demultiplexer_2_out0), .out1(Read_End), .in(chip_2), .sel(timer_1_finish));
  Timer timer_1 (.Time(multiplexer_1_out), .reset(crono_rst_2), .clock(Clock), .finish(timer_1_finish));
  or or_4 (RAM, Read_RAM, Write_RAM);
  or or_5 (or_5_out, demultiplexer_3_out0, crono_rst_1);
  D_Flip_Flop Load_Read (.clk(Clock), .D(Read_End), .Q(RAM_read_load), .reset(Reset));  // open: Qn, preset, en
  D_Flip_Flop Read_Inst (.clk(Clock), .D(or_5_out), .Q(chip_1), .reset(Reset));  // open: Qn, preset, en
  Timer timer_2 (.Time(Read_RAM_time), .reset(crono_rst_1), .clock(Clock), .finish(timer_2_finish));
  or or_6 (CS, chip_1, chip_2);
  Demultiplexer #(.enable("false")) demultiplexer_3 (
    .out0(demultiplexer_3_out0), .out1(E_inst), .in(chip_1), .sel(timer_2_finish));
  or or_7 (PC_Address, chip_1, crono_rst_1, E_PC);
  D_Flip_Flop Load_Inst (.clk(Clock), .D(E_inst), .Q(Load_Inst_q), .reset(Reset));  // open: Qn, preset, en
  Demultiplexer #(.enable("false")) demultiplexer_4 (
    .out0(demultiplexer_4_out0), .out1(demultiplexer_4_out1), .in(Load_Inst_q), .sel(halt));
  Demultiplexer #(.enable("false")) demultiplexer_5 (
    .out0(demultiplexer_5_out0), .out1(crono_rst_2), .in(demultiplexer_4_out0), .sel(RAM));
  or or_8 (or_8_out, demultiplexer_4_out1, End);
  D_Flip_Flop u_Halt (.clk(Clock), .D(or_8_out), .Q(End), .reset(Reset));  // open: Qn, preset, en
  and and_1 (R_W, Write_RAM, chip_2);

  // Other names for the same wires on the sheet: clk = Clock; R_W_t = crono_rst_2; R_W_RAM = R_W;
  //   Read_time[3:0] = Read_RAM_time; rst = Reset; Write_time[3:0] = Write_RAM_time
endmodule

module Timer (
  input  [3:0] Time,
  input  reset,
  input  clock,
  output finish
);

  wire [3:0] counter_1_q;

  Counter #(.width(4), .max('hf)) counter_1 (
    .count(1'b1), .Q(counter_1_q), .clk(clock), .clr(reset));  // open: load, D, carry
  Comparator #(.width(4)) comparator_1 (.a(Time), .b(counter_1_q), .eq(finish));  // open: gt, lt

  // Other names for the same wires on the sheet: clk = clock; rst = reset
endmodule
